# Fritzing sketch circuit layout for JoyLCD (saved by Fritzing 0.9.3b)
breadboards: 1

parts:
  R1 = Resistor [tolerance=±5% resistance=220 package=THT]
  Part1 = Arduino Uno (Rev3)
  LCD1 = LCD screen
  Part2 = Thumb Joystick
  R2 = TRIMPOT [package=3362u-2]

nets:
  5V: R1.Pin_0, Part1.5V, LCD1.VDD, Part2.VCC, R2.CW
  N1: R1.Pin_1, LCD1.LED+
  N2: Part1.A0, Part2.VERT
  N3: Part1.A1, Part2.HORZ
  N4: Part1.D8, Part2.SEL
  GND: Part1.GND, LCD1.VSS, LCD1.R/W, LCD1.LED-, Part2.GND, R2.CCW
  N5: Part1.D2, LCD1.RS
  N6: Part1.D3_PWM, LCD1.E
  N7: Part1.D4, LCD1.DB4
  N8: Part1.D5_PWM, LCD1.DB5
  N9: Part1.D6_PWM, LCD1.DB6
  N10: Part1.D7, LCD1.DB7
  N11: LCD1.V0, R2.WIPER

// code stored in the sketch: Joystick_with_LCD.ino
#include <LiquidCrystal.h> //Allows access to LCD functions

//sensor pins for joystick
const int y_dir = 0;
const int x_dir = 1;
const int push = 8;

//Storage for pin readings
int push_state = 0; 
int x_pos = 0;
int y_pos = 0;

//LCD pins
const int rs = 2; //register select pin
const int en = 3; //enable pin (connected to ground)
const int d4 = 4;
const int d5 = 5;
const int d6 = 6;
const int d7 = 7;

//LCD object initialization
LiquidCrystal my_lcd(rs,en,d4,d5,d6,d7);

//Index of cursor
int cursor_index = 0;

//string variable
char lcd_string = "A"; //Arbitrary value selected

void setup() {
  Serial.begin(9600);
  my_lcd.begin(16,2); //16 columns and 2 rows initialized
  
  pinMode(push, INPUT_PULLUP); //internal pullup resistor 
  
  pinMode(x_dir,INPUT);
  pinMode(y_dir,INPUT);
  
  my_lcd.print("Hello, User."); //16 character string maximum
  delay(3000); //3 second delay to allow user to read initial message
  
  my_lcd.clear();
  my_lcd.cursor(); //initializes cursor 
}

void loop() {
  
  push_state = digitalRead(push);
  x_pos = analogRead(x_dir);
  y_pos = analogRead(y_dir);
  
//Outputs joystick data to serial monitor
monitor_joy(); 

/*  The potentiometers in the joystick are mapped
 *from 0 to 1023 (10 bits), so the conditional 
 *values in the If statements and While statements 
 *were selected in order to match the joystick 
 *movement with the LCD commands.
 */

//move cursor to the left
 if(x_pos <= 300 && cursor_index > 0){

  cursor_index = cursor_index - 1;
  my_lcd.setCursor(cursor_index,0);
  delay(100); //Slows down movement of cursor
  }

//move cursor to the right 
 if(x_pos >= 700 && cursor_index < 16){
  
  cursor_index = 1+ cursor_index;
  my_lcd.setCursor(cursor_index,0);
  delay(100);
  }
  
//push button clears screen & resets cursor index
 if(push_state == 0){
  
  my_lcd.clear();
  cursor_index = 0;
  }
  
// increments through Ascii characters
 while(y_pos <200){
  
  lcd_string = lcd_string + 1;
  my_lcd.print(lcd_string);
  my_lcd.setCursor(cursor_index,0);
  delay(500);
  if (analogRead(y_dir) >200){
    break;
    }
  }
  
// decrements through Ascii characters
 while(y_pos > 800){
  
  lcd_string = lcd_string - 1;
  my_lcd.print(lcd_string);
  my_lcd.setCursor(cursor_index,0);
  delay(500);
    if (analogRead(y_dir) <800){
    break;
    }
  }
}

void monitor_joy(void){
  
Serial.print("Switch:  ");
Serial.print(push_state);
Serial.print("\n");

Serial.print("X-axis:  ");
Serial.print(x_pos);
Serial.print("\n");

Serial.print("Y-axis:  ");
Serial.print(y_pos);
Serial.print("\n\n");
  }
